# Fritzing sketch HotWater (saved by Fritzing 0.9.3b)
circuit board: 8.46667cm x 5.64444cm
breadboards: 1

parts:
  DS1 = DS18B20 1-Wire Temperature Sensor [part_number=DS18B20]
  DS2 = DS18B20 1-Wire Temperature Sensor [part_number=DS18B20]
  RGB_SMD_LED1 = SMD RGB LED (WS2812) [package=5050]
  WeMos_D1_Mini1 = WeMos D1 Mini
  R2 = Resistor [tolerance=±5% resistance=4.7k package="1206 [SMD]"]
  R3 = Resistor [tolerance=±5% resistance=220 package=THT]
  R4 = Resistor [tolerance=±5% resistance=10 package=THT]

nets:
  GND: DS1.GND, DS2.GND, RGB_SMD_LED1.VSS, R4.Pin_0
  N1: DS1.DQ, DS2.DQ, WeMos_D1_Mini1.D4, R2.Pin_0
  VDD: DS1.VDD, DS2.VDD, RGB_SMD_LED1.VCC, WeMos_D1_Mini1.3V3, R2.Pin_1
  N2: RGB_SMD_LED1.DIn, R3.Pin_0
  N3: WeMos_D1_Mini1.D6, R4.Pin_1
  N4: WeMos_D1_Mini1.RX, R3.Pin_1

notes:
  Water Flow Sensor
  Blue - data
  Black - ground
  Red - Vcc (3.3v)
